// Digital circuit NAND de 3 entradas.dig as structural Verilog
module NAND_de_3_entradas (
  input  A,
  input  B,
  input  C,
  output Y
);

  wire nfet_1_s, nfet_2_s;

  PFET pfet_1 (.G(A), .S(1'b1), .D(Y));
  PFET pfet_2 (.G(B), .S(1'b1), .D(Y));
  PFET pfet_3 (.G(C), .S(1'b1), .D(Y));
  NFET nfet_1 (.G(C), .D(Y), .S(nfet_1_s));
  NFET nfet_2 (.G(B), .D(nfet_1_s), .S(nfet_2_s));
  NFET nfet_3 (.G(A), .D(nfet_2_s), .S(1'b0));
endmodule
