// Digital circuit TriState_Buffer.dig as structural Verilog
module TriState_Buffer (
  input  Enable,
  input  Data,
  output Out
);

  wire and_1_out, nand_4_out, not_1_out;

  // NAnd nand_1 is placed but not wired
  // NAnd nand_2 is placed but not wired
  // NAnd nand_3 is placed but not wired
  nand nand_4 (nand_4_out, Enable, Data);
  and and_1 (and_1_out, Enable, not_1_out);
  not not_1 (not_1_out, Data);
  // NAnd nand_5 is placed but not wired
  FGPFET fgpfet_1 (.G(nand_4_out), .S(1'b1), .D(Out));
  NFET nfet_1 (.G(and_1_out), .D(Out), .S(1'b0));
endmodule
