// Digital circuit aaaa.dig as structural Verilog
module aaaa (
  input  in_1,
  input  in_2,
  input  in_3,
  input  in_4
);

  // Not not_1 has open pins: in=in_2, out=open
  // Not not_2 has open pins: in=in_3, out=open
  // XNOr xnor_1 is placed but not wired
  // XNOr xnor_2 is placed but not wired
  // Not not_3 has open pins: in=in_4, out=open
  // Or or_1 is placed but not wired
  // Or or_2 is placed but not wired
  // Or or_3 is placed but not wired
  // Or or_4 is placed but not wired
  // Or or_5 is placed but not wired
  // Or or_6 is placed but not wired
  // Or or_7 is placed but not wired
endmodule
