// Digital circuit alu_4bits.dig as structural Verilog
module alu_4bits (
  input  a_3,
  input  b_3,
  input  in_4,
  input  in_5,
  input  in_6,
  input  a_2,
  input  b_2,
  input  a_1,
  input  b_1,
  input  a_0,
  input  b_0,
  output F_3,
  output out_7,
  output out_8,
  output F_2,
  output F_1,
  output F_0
);

  wire and_1_out, and_2_out, and_3_out, and_4_out, and_5_out, and_6_out, and_7_out, and_8_out, and_9_out,
       and_10_out, and_11_out, and_12_out, and_13_out, and_14_out, and_15_out, and_16_out, and_17_out,
       and_18_out, and_19_out, and_20_out, and_21_out, and_22_out, and_23_out, and_24_out, and_25_out,
       and_26_out, and_27_out, and_28_out, and_29_out, and_30_out, and_31_out, and_32_out, and_33_out,
       not_1_out, not_2_out, not_3_out, not_4_out, not_5_out, not_6_out, not_7_out, not_8_out, not_9_out,
       not_10_out, not_11_out, not_12_out, not_13_out, not_14_out, not_15_out, not_16_out, not_17_out,
       not_18_out, not_19_out, not_20_out, not_21_out, not_22_out, not_23_out, not_24_out, not_25_out,
       not_26_out, not_27_out, not_28_out, or_1_out, or_3_out, or_4_out, or_5_out, or_6_out, or_7_out,
       or_8_out, or_9_out, or_10_out, or_11_out, or_12_out, or_13_out, or_14_out, or_15_out, or_16_out,
       or_17_out, or_18_out, or_19_out, or_20_out, xor_2_out, xor_4_out, xor_6_out, xor_8_out, xor_10_out;

  and and_1 (and_1_out, a_3, in_4);
  not not_1 (not_1_out, in_6);
  and and_2 (and_2_out, a_3, not_1_out);
  xor xor_1 (out_8, and_6_out, out_7);
  not not_2 (not_2_out, in_4);
  not not_3 (not_3_out, in_5);
  and and_3 (and_3_out, b_3, a_3, not_3_out);
  or or_1 (or_1_out, and_4_out, and_3_out, and_2_out, and_1_out);
  not not_4 (not_4_out, a_3);
  or or_2 (out_7, and_6_out, and_5_out);
  or or_3 (or_3_out, in_6, b_3);
  and and_4 (and_4_out, not_2_out, in_5, or_3_out, not_4_out);
  and and_5 (and_5_out, or_5_out, or_1_out);
  xor xor_2 (xor_2_out, or_5_out, or_1_out);
  and and_6 (and_6_out, or_7_out, xor_2_out);
  and and_7 (and_7_out, or_4_out, in_6, in_4);
  xor xor_3 (F_3, or_7_out, xor_2_out);
  not not_5 (not_5_out, in_5);
  not not_6 (not_6_out, in_6);
  or or_4 (or_4_out, not_7_out, in_5);
  or or_5 (or_5_out, and_8_out, and_7_out);
  not not_7 (not_7_out, b_3);
  and and_8 (and_8_out, b_3, in_4, not_5_out, not_6_out);
  not not_8 (not_8_out, in_6);
  and and_9 (and_9_out, a_2, in_4);
  not not_9 (not_9_out, in_4);
  not not_10 (not_10_out, in_5);
  and and_10 (and_10_out, a_2, not_8_out);
  or or_6 (or_6_out, and_13_out, and_11_out, and_10_out, and_9_out);
  not not_11 (not_11_out, a_2);
  and and_11 (and_11_out, b_2, a_2, not_10_out);
  or or_7 (or_7_out, and_14_out, and_12_out);
  or or_8 (or_8_out, in_6, b_2);
  and and_12 (and_12_out, or_10_out, or_6_out);
  and and_13 (and_13_out, not_9_out, in_5, or_8_out, not_11_out);
  and and_14 (and_14_out, or_13_out, xor_4_out);
  and and_15 (and_15_out, or_9_out, in_6, in_4);
  xor xor_4 (xor_4_out, or_10_out, or_6_out);
  xor xor_5 (F_2, or_13_out, xor_4_out);
  or or_9 (or_9_out, not_12_out, in_5);
  not not_12 (not_12_out, b_2);
  not not_13 (not_13_out, in_5);
  not not_14 (not_14_out, in_6);
  or or_10 (or_10_out, and_16_out, and_15_out);
  and and_16 (and_16_out, b_2, in_4, not_13_out, not_14_out);
  not not_15 (not_15_out, in_6);
  and and_17 (and_17_out, a_1, in_4);
  not not_16 (not_16_out, in_4);
  not not_17 (not_17_out, in_5);
  and and_18 (and_18_out, a_1, not_15_out);
  not not_18 (not_18_out, a_1);
  and and_19 (and_19_out, b_1, a_1, not_17_out);
  or or_11 (or_11_out, and_21_out, and_19_out, and_18_out, and_17_out);
  or or_12 (or_12_out, in_6, b_1);
  and and_20 (and_20_out, or_15_out, or_11_out);
  or or_13 (or_13_out, and_22_out, and_20_out);
  and and_21 (and_21_out, not_16_out, in_5, or_12_out, not_18_out);
  and and_22 (and_22_out, or_17_out, xor_6_out);
  xor xor_6 (xor_6_out, or_15_out, or_11_out);
  xor xor_7 (F_1, or_17_out, xor_6_out);
  or or_14 (or_14_out, not_19_out, in_5);
  and and_23 (and_23_out, or_14_out, in_6, in_4);
  not not_19 (not_19_out, b_1);
  not not_20 (not_20_out, in_5);
  not not_21 (not_21_out, in_6);
  or or_15 (or_15_out, and_24_out, and_23_out);
  and and_24 (and_24_out, b_1, in_4, not_20_out, not_21_out);
  and and_25 (and_25_out, a_0, in_4);
  not not_22 (not_22_out, in_4);
  not not_23 (not_23_out, in_6);
  and and_26 (and_26_out, a_0, not_23_out);
  not not_24 (not_24_out, in_5);
  not not_25 (not_25_out, a_0);
  and and_27 (and_27_out, b_0, a_0, not_24_out);
  or or_16 (or_16_out, and_28_out, and_27_out, and_26_out, and_25_out);
  or or_17 (or_17_out, and_30_out, and_29_out);
  or or_18 (or_18_out, in_6, b_0);
  and and_28 (and_28_out, not_22_out, in_5, or_18_out, not_25_out);
  and and_29 (and_29_out, or_20_out, or_16_out);
  xor xor_8 (xor_8_out, or_20_out, or_16_out);
  and and_30 (and_30_out, and_32_out, xor_8_out);
  xor xor_9 (F_0, and_32_out, xor_8_out);
  and and_31 (and_31_out, or_19_out, in_6, in_4);
  not not_26 (not_26_out, in_5);
  not not_27 (not_27_out, in_6);
  or or_19 (or_19_out, not_28_out, in_5);
  or or_20 (or_20_out, and_33_out, and_31_out);
  not not_28 (not_28_out, b_0);
  and and_32 (and_32_out, in_4, xor_10_out);
  and and_33 (and_33_out, b_0, in_4, not_26_out, not_27_out);
  xor xor_10 (xor_10_out, in_5, in_6);

  // Other names for the same wires on the sheet: Sel0 = in_6; Sel1 = in_5; Sel2 = in_4
endmodule
