// Digital circuit counter_register_4bits.dig as structural Verilog
module counter_register_4bits (
  input  load,
  input  set,
  input  clear,
  input  clk,
  output out_5,
  output Overflow,
  output counter,
  output out_8,
  output out_9,
  output out_10
);

  wire and_2_out, and_3_out, and_4_out, multiplexer_1_out, multiplexer_2_out, multiplexer_3_out,
       multiplexer_4_out, xor_1_out, xor_2_out, xor_3_out, xor_4_out;

  and and_1 (Overflow, out_5, and_2_out);
  xor xor_1 (xor_1_out, out_5, and_2_out);
  Multiplexer multiplexer_1 (.sel(load), .in_0(out_5), .in_1(xor_1_out), .out(multiplexer_1_out));
  D_FF_AS d_ff_as_1 (.Set(set), .D(multiplexer_1_out), .C(clk), .Clr(clear), .Q(out_5));  // open: nQ
  and and_2 (and_2_out, out_8, and_3_out);
  xor xor_2 (xor_2_out, out_8, and_3_out);
  Multiplexer multiplexer_2 (.sel(load), .in_0(out_8), .in_1(xor_2_out), .out(multiplexer_2_out));
  D_FF_AS d_ff_as_2 (.Set(set), .D(multiplexer_2_out), .C(clk), .Clr(clear), .Q(out_8));  // open: nQ
  and and_3 (and_3_out, out_9, and_4_out);
  xor xor_3 (xor_3_out, out_9, and_4_out);
  Multiplexer multiplexer_3 (.sel(load), .in_0(out_9), .in_1(xor_3_out), .out(multiplexer_3_out));
  D_FF_AS d_ff_as_3 (.Set(set), .D(multiplexer_3_out), .C(clk), .Clr(clear), .Q(out_9));  // open: nQ
  and and_4 (and_4_out, out_10, counter);
  xor xor_4 (xor_4_out, out_10, counter);
  Multiplexer multiplexer_4 (.sel(load), .in_0(out_10), .in_1(xor_4_out), .out(multiplexer_4_out));
  D_FF_AS d_ff_as_4 (.Set(set), .D(multiplexer_4_out), .C(clk), .Clr(clear), .Q(out_10));  // open: nQ
endmodule
