// Digital circuit d flipflop with set and reset.dig as structural Verilog
module d_flipflop_with_set_and_reset (
  input  D,
  input  set,
  input  clear,
  input  clk,
  output Q,
  output Q_2
);

  wire nand_1_out, nand_2_out, nand_3_out, nand_4_out, nand_5_out, nand_6_out, not_1_out, not_2_out,
       not_3_out, not_4_out, not_5_out;

  not not_1 (not_1_out, D);
  not not_2 (not_2_out, clk);
  not not_3 (not_3_out, set);
  nand nand_1 (nand_1_out, D, not_2_out);
  nand nand_2 (nand_2_out, not_2_out, not_1_out);
  not not_4 (not_4_out, clear);
  nand nand_3 (nand_3_out, not_3_out, nand_1_out, nand_4_out);
  nand nand_4 (nand_4_out, nand_3_out, nand_2_out, not_4_out);
  not not_5 (not_5_out, nand_3_out);
  nand nand_5 (nand_5_out, nand_3_out, clk);
  nand nand_6 (nand_6_out, clk, not_5_out);
  nand nand_7 (Q, not_3_out, nand_5_out, Q_2);
  nand nand_8 (Q_2, Q, nand_6_out, not_4_out);

  // Notes on the sheet:
  //   set: set
  //   clk: Hz: 5
endmodule
