// Digital circuit d latch.dig as structural Verilog
module d_latch (
  input  S,
  input  R,
  input  Enable,
  input  in_8,
  output Q,
  output Q_2,
  output Q_3,
  output Q_4
);

  wire nand_1_out, nand_2_out, not_1_out;

  nand nand_1 (nand_1_out, S, Enable);
  nand nand_2 (nand_2_out, Enable, R);
  not not_1 (not_1_out, in_8);
  nand nand_3 (Q, nand_1_out, Q_2);
  nand nand_4 (Q_2, Q, nand_2_out);
  nand nand_5 (Q_3, not_1_out, Q_4);
  nand nand_6 (Q_4, Q_3, in_8);
endmodule
