// Digital circuit d_latch_v2.dig as structural Verilog
module d_latch_v2 (
  input  Enable,
  input  D,
  input  set,
  input  clear,
  input  select,
  output Q
);

  wire multiplexer_1_out, nand_1_out, nand_2_out, nand_4_out, not_1_out;

  Multiplexer multiplexer_1 (.sel(select), .in_0(Q), .in_1(D), .out(multiplexer_1_out));
  not not_1 (not_1_out, multiplexer_1_out);
  nand nand_1 (nand_1_out, multiplexer_1_out, Enable);
  nand nand_2 (nand_2_out, Enable, not_1_out);
  nand nand_3 (Q, set, nand_1_out, nand_4_out);
  nand nand_4 (nand_4_out, Q, nand_2_out, clear);
endmodule
