// Digital circuit full_adder_1bit.dig as structural Verilog
module full_adder_1bit (
  input  x_i,
  input  y_i,
  input  C_i,
  output S_i,
  output C_i_plus_1
);

  wire and_1_out, and_2_out, xor_1_out;

  or or_1 (C_i_plus_1, and_2_out, and_1_out);
  and and_1 (and_1_out, y_i, x_i);
  xor xor_1 (xor_1_out, y_i, x_i);
  and and_2 (and_2_out, C_i, xor_1_out);
  xor xor_2 (S_i, C_i, xor_1_out);
endmodule
