// Digital circuit full_adder_4bits.dig as structural Verilog
module full_adder_4bits (
  input  x_i,
  input  y_i,
  input  x_i_2,
  input  y_i_2,
  input  x_i_3,
  input  y_i_3,
  input  x_i_4,
  input  y_i_4,
  input  C_i,
  output S_i,
  output C_i_plus_1,
  output S_i_2,
  output S_i_3,
  output S_i_4
);

  wire and_1_out, and_2_out, and_3_out, and_4_out, and_5_out, and_6_out, and_7_out, and_8_out, or_2_out,
       or_3_out, or_4_out, xor_1_out, xor_3_out, xor_5_out, xor_7_out;

  or or_1 (C_i_plus_1, and_2_out, and_1_out);
  and and_1 (and_1_out, y_i, x_i);
  xor xor_1 (xor_1_out, y_i, x_i);
  and and_2 (and_2_out, or_2_out, xor_1_out);
  xor xor_2 (S_i, or_2_out, xor_1_out);
  or or_2 (or_2_out, and_4_out, and_3_out);
  and and_3 (and_3_out, y_i_2, x_i_2);
  xor xor_3 (xor_3_out, y_i_2, x_i_2);
  and and_4 (and_4_out, or_3_out, xor_3_out);
  xor xor_4 (S_i_2, or_3_out, xor_3_out);
  and and_5 (and_5_out, y_i_3, x_i_3);
  or or_3 (or_3_out, and_6_out, and_5_out);
  and and_6 (and_6_out, or_4_out, xor_5_out);
  xor xor_5 (xor_5_out, y_i_3, x_i_3);
  xor xor_6 (S_i_3, or_4_out, xor_5_out);
  or or_4 (or_4_out, and_8_out, and_7_out);
  and and_7 (and_7_out, y_i_4, x_i_4);
  and and_8 (and_8_out, C_i, xor_7_out);
  xor xor_7 (xor_7_out, y_i_4, x_i_4);
  xor xor_8 (S_i_4, C_i, xor_7_out);
endmodule
