// Digital circuit multiplexer(2_1).dig as structural Verilog
module multiplexer_2_1 (
  input  D_0,
  input  Sel,
  input  D_1,
  output Out
);

  wire and_1_out, and_2_out, not_1_out;

  not not_1 (not_1_out, Sel);
  and and_1 (and_1_out, D_0, not_1_out);
  and and_2 (and_2_out, Sel, D_1);
  or or_1 (Out, and_1_out, and_2_out);
endmodule
