// Digital circuit multiplexer(4_1).dig as structural Verilog
module multiplexer_4_1 (
  input  D_3,
  input  D_2,
  input  D_1,
  input  D_0,
  input  in_5,
  input  in_6,
  output out
);

  wire and_1_out, and_2_out, and_3_out, and_4_out, not_1_out, not_2_out;

  not not_1 (not_1_out, in_5);
  and and_1 (and_1_out, D_3, in_5, in_6);
  and and_2 (and_2_out, D_2, in_5, not_2_out);
  and and_3 (and_3_out, D_1, not_1_out, in_6);
  and and_4 (and_4_out, D_0, not_1_out, not_2_out);
  not not_2 (not_2_out, in_6);
  or or_1 (out, and_1_out, and_2_out, and_3_out, and_4_out);
endmodule
