// Digital circuit register_1bit.dig as structural Verilog
module register_1bit (
  input  D,
  input  set,
  input  clear,
  input  clk,
  input  Enable,
  input  d_2,
  input  load,
  input  in_9,
  input  in_11,
  input  clk_2,
  output Q,
  output out_10
);

  wire multiplexer_1_out, multiplexer_2_out, nand_1_out, nand_2_out, nand_3_out, nand_4_out, nand_5_out,
       nand_6_out, nand_8_out, not_1_out, not_2_out, not_3_out, not_4_out, not_5_out;

  Multiplexer multiplexer_1 (.sel(Enable), .in_0(Q), .in_1(D), .out(multiplexer_1_out));
  not not_1 (not_1_out, multiplexer_1_out);
  not not_2 (not_2_out, clk);
  Multiplexer multiplexer_2 (.sel(load), .in_0(out_10), .in_1(d_2), .out(multiplexer_2_out));
  not not_3 (not_3_out, set);
  nand nand_1 (nand_1_out, multiplexer_1_out, not_2_out);
  nand nand_2 (nand_2_out, not_2_out, not_1_out);
  not not_4 (not_4_out, clear);
  nand nand_3 (nand_3_out, not_3_out, nand_1_out, nand_4_out);
  nand nand_4 (nand_4_out, nand_3_out, nand_2_out, not_4_out);
  D_FF_AS d_ff_as_1 (.Set(in_9), .D(multiplexer_2_out), .C(clk_2), .Clr(in_11), .Q(out_10));  // open: nQ
  not not_5 (not_5_out, nand_3_out);
  nand nand_5 (nand_5_out, nand_3_out, clk);
  nand nand_6 (nand_6_out, clk, not_5_out);
  nand nand_7 (Q, not_3_out, nand_5_out, nand_8_out);
  nand nand_8 (nand_8_out, Q, nand_6_out, not_4_out);

  // Notes on the sheet:
  //   set: set
  //   clk: Hz: 10
  //   clk_2: Hz: 10
endmodule
