// Digital circuit register_4bit.dig as structural Verilog
module register_4bit (
  input  D3,
  input  load,
  input  set,
  input  clear,
  input  clk,
  input  D2,
  input  D1,
  input  D0,
  output out_6,
  output out_7,
  output out_9,
  output out_11
);

  wire multiplexer_1_out, multiplexer_2_out, multiplexer_3_out, multiplexer_4_out;

  Multiplexer multiplexer_1 (.sel(load), .in_0(out_6), .in_1(D3), .out(multiplexer_1_out));
  D_FF_AS d_ff_as_1 (.Set(set), .D(multiplexer_1_out), .C(clk), .Clr(clear), .Q(out_6));  // open: nQ
  Multiplexer multiplexer_2 (.sel(load), .in_0(out_7), .in_1(D2), .out(multiplexer_2_out));
  D_FF_AS d_ff_as_2 (.Set(set), .D(multiplexer_2_out), .C(clk), .Clr(clear), .Q(out_7));  // open: nQ
  Multiplexer multiplexer_3 (.sel(load), .in_0(out_9), .in_1(D1), .out(multiplexer_3_out));
  D_FF_AS d_ff_as_3 (.Set(set), .D(multiplexer_3_out), .C(clk), .Clr(clear), .Q(out_9));  // open: nQ
  Multiplexer multiplexer_4 (.sel(load), .in_0(out_11), .in_1(D0), .out(multiplexer_4_out));
  D_FF_AS d_ff_as_4 (.Set(set), .D(multiplexer_4_out), .C(clk), .Clr(clear), .Q(out_11));  // open: nQ

  // Notes on the sheet:
  //   clk: Hz: 2
endmodule
