// Digital circuit simpleport_driver.dig as structural Verilog
module simpleport_driver (
  input  load,
  input  set,
  input  clear,
  input  clk,
  input  DirControl_PA3,
  input  load_2,
  input  set_2,
  input  clear_2,
  input  DirControl_PA2,
  input  DirControl_PA1,
  input  DirControl_PA0,
  input  Output_PA3,
  input  load_3,
  input  set_3,
  input  clear_3,
  input  Output_PA2,
  input  Output_PA1,
  input  Output_PA0,
  input  in_23,
  input  in_25,
  input  in_27,
  input  in_29,
  output out_5,
  output out_6,
  output out_7,
  output out_8,
  output out_24,
  output out_26,
  output out_28,
  output out_30
);

  wire multiplexer_1_out, multiplexer_2_out, multiplexer_3_out, multiplexer_4_out, multiplexer_5_out,
       multiplexer_6_out, multiplexer_7_out, multiplexer_8_out, multiplexer_9_out, multiplexer_10_out,
       multiplexer_11_out, multiplexer_12_out, PA0_DCtrl, PA0_Input, PA0_Output, PA1_DCtrl, PA1_Input,
       PA1_Output, PA2_DCtrl, PA2_Input, PA2_Output, PA3_DCtrl, PA3_Input, PA3_Output;

  Multiplexer multiplexer_1 (.sel(load), .in_0(out_5), .in_1(PA3_Input), .out(multiplexer_1_out));
  Multiplexer multiplexer_2 (.sel(load_2), .in_0(PA3_DCtrl), .in_1(DirControl_PA3), .out(multiplexer_2_out));
  Multiplexer multiplexer_3 (.sel(load_3), .in_0(PA3_Output), .in_1(Output_PA3), .out(multiplexer_3_out));
  D_FF_AS d_ff_as_1 (.Set(set), .D(multiplexer_1_out), .C(clk), .Clr(clear), .Q(out_5));  // open: nQ
  D_FF_AS d_ff_as_2 (.Set(set_3), .D(multiplexer_3_out), .C(clk), .Clr(clear_3), .Q(PA3_Output));  // open: nQ
  D_FF_AS d_ff_as_3 (.Set(set_2), .D(multiplexer_2_out), .C(clk), .Clr(clear_2), .Q(PA3_DCtrl));  // open: nQ
  Multiplexer multiplexer_4 (.sel(load), .in_0(out_6), .in_1(PA2_Input), .out(multiplexer_4_out));
  Multiplexer multiplexer_5 (.sel(load_2), .in_0(PA2_DCtrl), .in_1(DirControl_PA2), .out(multiplexer_5_out));
  Multiplexer multiplexer_6 (.sel(load_3), .in_0(PA2_Output), .in_1(Output_PA2), .out(multiplexer_6_out));
  D_FF_AS d_ff_as_4 (.Set(set), .D(multiplexer_4_out), .C(clk), .Clr(clear), .Q(out_6));  // open: nQ
  D_FF_AS d_ff_as_5 (.Set(set_2), .D(multiplexer_5_out), .C(clk), .Clr(clear_2), .Q(PA2_DCtrl));  // open: nQ
  D_FF_AS d_ff_as_6 (.Set(set_3), .D(multiplexer_6_out), .C(clk), .Clr(clear_3), .Q(PA2_Output));  // open: nQ
  Multiplexer multiplexer_7 (.sel(load), .in_0(out_7), .in_1(PA1_Input), .out(multiplexer_7_out));
  Multiplexer multiplexer_8 (.sel(load_3), .in_0(PA1_Output), .in_1(Output_PA1), .out(multiplexer_8_out));
  Multiplexer multiplexer_9 (.sel(load_2), .in_0(PA1_DCtrl), .in_1(DirControl_PA1), .out(multiplexer_9_out));
  D_FF_AS d_ff_as_7 (.Set(set), .D(multiplexer_7_out), .C(clk), .Clr(clear), .Q(out_7));  // open: nQ
  D_FF_AS d_ff_as_8 (.Set(set_2), .D(multiplexer_9_out), .C(clk), .Clr(clear_2), .Q(PA1_DCtrl));  // open: nQ
  D_FF_AS d_ff_as_9 (.Set(set_3), .D(multiplexer_8_out), .C(clk), .Clr(clear_3), .Q(PA1_Output));  // open: nQ
  Multiplexer multiplexer_10 (.sel(load), .in_0(out_8), .in_1(PA0_Input), .out(multiplexer_10_out));
  Multiplexer multiplexer_11 (.sel(load_2), .in_0(PA0_DCtrl), .in_1(DirControl_PA0), .out(multiplexer_11_out));
  Multiplexer multiplexer_12 (.sel(load_3), .in_0(PA0_Output), .in_1(Output_PA0), .out(multiplexer_12_out));
  D_FF_AS d_ff_as_10 (.Set(set), .D(multiplexer_10_out), .C(clk), .Clr(clear), .Q(out_8));  // open: nQ
  D_FF_AS d_ff_as_11 (.Set(set_2), .D(multiplexer_11_out), .C(clk), .Clr(clear_2), .Q(PA0_DCtrl));  // open: nQ
  D_FF_AS d_ff_as_12 (.Set(set_3), .D(multiplexer_12_out), .C(clk), .Clr(clear_3), .Q(PA0_Output));  // open: nQ
  assign PA0_Input = ~PA0_DCtrl ? in_23 : 1'bz;  // DriverInvSel driverinvsel_1
  assign out_24 = PA0_DCtrl ? PA0_Output : 1'bz;  // Driver driver_1
  assign PA1_Input = ~PA1_DCtrl ? in_25 : 1'bz;  // DriverInvSel driverinvsel_2
  assign out_26 = PA1_DCtrl ? PA1_Output : 1'bz;  // Driver driver_2
  assign PA2_Input = ~PA2_DCtrl ? in_27 : 1'bz;  // DriverInvSel driverinvsel_3
  assign out_28 = PA2_DCtrl ? PA2_Output : 1'bz;  // Driver driver_3
  assign PA3_Input = ~PA3_DCtrl ? in_29 : 1'bz;  // DriverInvSel driverinvsel_4
  assign out_30 = PA3_DCtrl ? PA3_Output : 1'bz;  // Driver driver_4

  // Notes on the sheet:
  //   Output Data Register
  //   Input Data Register
  //   Control Dir Register
endmodule
