// Digital circuit demultiplexor.dig as structural Verilog
module demultiplexor (
  input  bit2,
  input  bit1,
  input  Data,
  output Output1,
  output Output2,
  output Output3,
  output Output4
);

  wire not_1_out, not_2_out;

  not not_1 (not_1_out, bit2);
  not not_2 (not_2_out, bit1);
  and and_1 (Output1, not_1_out, not_2_out, Data);
  and and_2 (Output2, not_1_out, bit1, Data);
  and and_3 (Output3, bit2, not_2_out, Data);
  and and_4 (Output4, bit2, bit1, Data);
endmodule
