// Digital circuit mulplexer_from_tristate_buffer.dig as structural Verilog
module mulplexer_from_tristate_buffer (
  input  B,
  input  A,
  input  select,
  output \output 
);

  wire and_1_out, and_2_out, nand_1_out, nand_2_out, not_1_out, not_2_out, not_3_out;

  not not_1 (not_1_out, select);
  nand nand_1 (nand_1_out, not_1_out, A);
  and and_1 (and_1_out, not_1_out, not_2_out);
  not not_2 (not_2_out, A);
  nand nand_2 (nand_2_out, select, B);
  and and_2 (and_2_out, select, not_3_out);
  not not_3 (not_3_out, B);
  FGPFET fgpfet_1 (.G(nand_1_out), .S(1'b1), .D(\output ));
  NFET nfet_1 (.G(and_1_out), .D(\output ), .S(1'b0));
  FGPFET fgpfet_2 (.G(nand_2_out), .S(1'b1), .D(\output ));
  NFET nfet_2 (.G(and_2_out), .D(\output ), .S(1'b0));
endmodule
