// Digital circuit port_driver.dig as structural Verilog
module port_driver (
  input  load,
  input  set,
  input  clear,
  input  DirControl_PA31,
  input  load_2,
  input  set_2,
  input  clear_2,
  input  DirControl_PA30,
  input  DirControl_PA21,
  input  DirControl_PA20,
  input  Output_PA3,
  input  load_3,
  input  set_3,
  input  clear_3,
  input  Output_PA2,
  input  Output_PA1,
  input  Output_PA0,
  input  DirControl_PA11,
  input  DirControl_PA10,
  input  DirControl_PA01,
  input  DirControl_PA00,
  input  A_Output_PA3,
  input  load_4,
  input  set_4,
  input  clear_4,
  input  A_Output_PA2,
  input  A_Output_PA1,
  input  A_Output_PA0,
  input  load_5,
  input  set_5,
  input  clear_5,
  input  clk,
  input  in_41,
  input  in_43,
  input  in_45,
  input  in_47,
  output out_4,
  output out_5,
  output out_6,
  output out_7,
  output out_37,
  output out_38,
  output out_39,
  output out_40,
  output out_42,
  output out_44,
  output out_46,
  output out_48
);

  wire driverinvsel_2_out, driverinvsel_4_out, driverinvsel_5_out, driverinvsel_6_out, driverinvsel_8_out,
       driverinvsel_10_out, driverinvsel_11_out, driverinvsel_12_out, multiplexer_1_out, multiplexer_2_out,
       multiplexer_3_out, multiplexer_4_out, multiplexer_5_out, multiplexer_6_out, multiplexer_7_out,
       multiplexer_8_out, multiplexer_9_out, multiplexer_10_out, multiplexer_11_out, multiplexer_12_out,
       multiplexer_13_out, multiplexer_14_out, multiplexer_15_out, multiplexer_16_out, multiplexer_17_out,
       multiplexer_18_out, multiplexer_19_out, multiplexer_20_out, multiplexer_21_out, multiplexer_22_out,
       multiplexer_23_out, multiplexer_24_out, PA0_A_Output, PA0_ADC_Input, PA0_DCtrl_0, PA0_DCtrl_1,
       PA0_Input, PA0_Output, PA1_A_Output, PA1_ADC_Input, PA1_DCtrl_0, PA1_DCtrl_1, PA1_Input, PA1_Output,
       PA2_A_Output, PA2_ADC_Input, PA2_DCtrl_0, PA2_DCtrl_1, PA2_Input, PA2_Output, PA3_A_Output,
       PA3_ADC_Input, PA3_DCtrl_0, PA3_DCtrl_1, PA3_Input, PA3_Output;

  Multiplexer multiplexer_1 (.sel(load_5), .in_0(out_37), .in_1(PA3_Input), .out(multiplexer_1_out));
  Multiplexer multiplexer_2 (.sel(load), .in_0(out_4), .in_1(PA3_ADC_Input), .out(multiplexer_2_out));
  Multiplexer multiplexer_3 (.sel(load_2), .in_0(PA3_DCtrl_1), .in_1(DirControl_PA31), .out(multiplexer_3_out));
  Multiplexer multiplexer_4 (.sel(load_3), .in_0(PA3_Output), .in_1(Output_PA3), .out(multiplexer_4_out));
  Multiplexer multiplexer_5 (.sel(load_4), .in_0(PA3_A_Output), .in_1(A_Output_PA3), .out(multiplexer_5_out));
  D_FF_AS d_ff_as_1 (.Set(set_5), .D(multiplexer_1_out), .C(clk), .Clr(clear_5), .Q(out_37));  // open: nQ
  D_FF_AS d_ff_as_2 (.Set(set), .D(multiplexer_2_out), .C(clk), .Clr(clear), .Q(out_4));  // open: nQ
  D_FF_AS d_ff_as_3 (.Set(set_3), .D(multiplexer_4_out), .C(clk), .Clr(clear_3), .Q(PA3_Output));  // open: nQ
  D_FF_AS d_ff_as_4 (.Set(set_4), .D(multiplexer_5_out), .C(clk), .Clr(clear_4), .Q(PA3_A_Output));  // open: nQ
  D_FF_AS d_ff_as_5 (.Set(set_2), .D(multiplexer_3_out), .C(clk), .Clr(clear_2), .Q(PA3_DCtrl_1));  // open: nQ
  Multiplexer multiplexer_6 (.sel(load_5), .in_0(out_38), .in_1(PA2_Input), .out(multiplexer_6_out));
  Multiplexer multiplexer_7 (.sel(load), .in_0(out_5), .in_1(PA2_ADC_Input), .out(multiplexer_7_out));
  Multiplexer multiplexer_8 (.sel(load_2), .in_0(PA3_DCtrl_0), .in_1(DirControl_PA30), .out(multiplexer_8_out));
  Multiplexer multiplexer_9 (.sel(load_3), .in_0(PA2_Output), .in_1(Output_PA2), .out(multiplexer_9_out));
  Multiplexer multiplexer_10 (.sel(load_4), .in_0(PA2_A_Output), .in_1(A_Output_PA2), .out(multiplexer_10_out));
  D_FF_AS d_ff_as_6 (.Set(set), .D(multiplexer_7_out), .C(clk), .Clr(clear), .Q(out_5));  // open: nQ
  D_FF_AS d_ff_as_7 (.Set(set_2), .D(multiplexer_8_out), .C(clk), .Clr(clear_2), .Q(PA3_DCtrl_0));  // open: nQ
  D_FF_AS d_ff_as_8 (.Set(set_5), .D(multiplexer_6_out), .C(clk), .Clr(clear_5), .Q(out_38));  // open: nQ
  D_FF_AS d_ff_as_9 (.Set(set_3), .D(multiplexer_9_out), .C(clk), .Clr(clear_3), .Q(PA2_Output));  // open: nQ
  D_FF_AS d_ff_as_10 (.Set(set_4), .D(multiplexer_10_out), .C(clk), .Clr(clear_4), .Q(PA2_A_Output));  // open: nQ
  Multiplexer multiplexer_11 (.sel(load_2), .in_0(PA2_DCtrl_1), .in_1(DirControl_PA21), .out(multiplexer_11_out));
  Multiplexer multiplexer_12 (.sel(load_5), .in_0(out_39), .in_1(PA1_Input), .out(multiplexer_12_out));
  Multiplexer multiplexer_13 (.sel(load), .in_0(out_6), .in_1(PA1_ADC_Input), .out(multiplexer_13_out));
  Multiplexer multiplexer_14 (.sel(load_3), .in_0(PA1_Output), .in_1(Output_PA1), .out(multiplexer_14_out));
  Multiplexer multiplexer_15 (.sel(load_4), .in_0(PA1_A_Output), .in_1(A_Output_PA1), .out(multiplexer_15_out));
  D_FF_AS d_ff_as_11 (.Set(set_2), .D(multiplexer_11_out), .C(clk), .Clr(clear_2), .Q(PA2_DCtrl_1));  // open: nQ
  D_FF_AS d_ff_as_12 (.Set(set_5), .D(multiplexer_12_out), .C(clk), .Clr(clear_5), .Q(out_39));  // open: nQ
  D_FF_AS d_ff_as_13 (.Set(set), .D(multiplexer_13_out), .C(clk), .Clr(clear), .Q(out_6));  // open: nQ
  D_FF_AS d_ff_as_14 (.Set(set_3), .D(multiplexer_14_out), .C(clk), .Clr(clear_3), .Q(PA1_Output));  // open: nQ
  D_FF_AS d_ff_as_15 (.Set(set_4), .D(multiplexer_15_out), .C(clk), .Clr(clear_4), .Q(PA1_A_Output));  // open: nQ
  Multiplexer multiplexer_16 (.sel(load_2), .in_0(PA2_DCtrl_0), .in_1(DirControl_PA20), .out(multiplexer_16_out));
  Multiplexer multiplexer_17 (.sel(load), .in_0(out_7), .in_1(PA0_ADC_Input), .out(multiplexer_17_out));
  D_FF_AS d_ff_as_16 (.Set(set_2), .D(multiplexer_16_out), .C(clk), .Clr(clear_2), .Q(PA2_DCtrl_0));  // open: nQ
  Multiplexer multiplexer_18 (.sel(load_5), .in_0(out_40), .in_1(PA0_Input), .out(multiplexer_18_out));
  Multiplexer multiplexer_19 (.sel(load_3), .in_0(PA0_Output), .in_1(Output_PA0), .out(multiplexer_19_out));
  Multiplexer multiplexer_20 (.sel(load_4), .in_0(PA0_A_Output), .in_1(A_Output_PA0), .out(multiplexer_20_out));
  D_FF_AS d_ff_as_17 (.Set(set_5), .D(multiplexer_18_out), .C(clk), .Clr(clear_5), .Q(out_40));  // open: nQ
  D_FF_AS d_ff_as_18 (.Set(set), .D(multiplexer_17_out), .C(clk), .Clr(clear), .Q(out_7));  // open: nQ
  Multiplexer multiplexer_21 (.sel(load_2), .in_0(PA1_DCtrl_1), .in_1(DirControl_PA11), .out(multiplexer_21_out));
  D_FF_AS d_ff_as_19 (.Set(set_3), .D(multiplexer_19_out), .C(clk), .Clr(clear_3), .Q(PA0_Output));  // open: nQ
  D_FF_AS d_ff_as_20 (.Set(set_4), .D(multiplexer_20_out), .C(clk), .Clr(clear_4), .Q(PA0_A_Output));  // open: nQ
  D_FF_AS d_ff_as_21 (.Set(set_2), .D(multiplexer_21_out), .C(clk), .Clr(clear_2), .Q(PA1_DCtrl_1));  // open: nQ
  Multiplexer multiplexer_22 (.sel(load_2), .in_0(PA1_DCtrl_0), .in_1(DirControl_PA10), .out(multiplexer_22_out));
  D_FF_AS d_ff_as_22 (.Set(set_2), .D(multiplexer_22_out), .C(clk), .Clr(clear_2), .Q(PA1_DCtrl_0));  // open: nQ
  assign PA0_Input = ~PA0_DCtrl_1 ? driverinvsel_5_out : 1'bz;  // DriverInvSel driverinvsel_1
  assign PA0_ADC_Input = PA0_DCtrl_1 ? driverinvsel_5_out : 1'bz;  // Driver driver_1
  assign driverinvsel_2_out = ~PA0_DCtrl_1 ? PA0_Output : 1'bz;  // DriverInvSel driverinvsel_2
  assign driverinvsel_2_out = PA0_DCtrl_1 ? PA0_A_Output : 1'bz;  // Driver driver_2
  assign PA2_Input = ~PA2_DCtrl_1 ? driverinvsel_6_out : 1'bz;  // DriverInvSel driverinvsel_3
  assign PA2_ADC_Input = PA2_DCtrl_1 ? driverinvsel_6_out : 1'bz;  // Driver driver_3
  assign driverinvsel_4_out = ~PA2_DCtrl_1 ? PA2_Output : 1'bz;  // DriverInvSel driverinvsel_4
  assign driverinvsel_4_out = PA2_DCtrl_1 ? PA2_A_Output : 1'bz;  // Driver driver_4
  Multiplexer multiplexer_23 (.sel(load_2), .in_0(PA0_DCtrl_1), .in_1(DirControl_PA01), .out(multiplexer_23_out));
  assign driverinvsel_5_out = ~PA0_DCtrl_0 ? in_41 : 1'bz;  // DriverInvSel driverinvsel_5
  assign out_42 = PA0_DCtrl_0 ? driverinvsel_2_out : 1'bz;  // Driver driver_5
  assign driverinvsel_6_out = ~PA2_DCtrl_0 ? in_43 : 1'bz;  // DriverInvSel driverinvsel_6
  assign out_44 = PA2_DCtrl_0 ? driverinvsel_4_out : 1'bz;  // Driver driver_6
  D_FF_AS d_ff_as_23 (.Set(set_2), .D(multiplexer_23_out), .C(clk), .Clr(clear_2), .Q(PA0_DCtrl_1));  // open: nQ
  Multiplexer multiplexer_24 (.sel(load_2), .in_0(PA0_DCtrl_0), .in_1(DirControl_PA00), .out(multiplexer_24_out));
  D_FF_AS d_ff_as_24 (.Set(set_2), .D(multiplexer_24_out), .C(clk), .Clr(clear_2), .Q(PA0_DCtrl_0));  // open: nQ
  assign PA1_Input = ~PA1_DCtrl_1 ? driverinvsel_11_out : 1'bz;  // DriverInvSel driverinvsel_7
  assign PA1_ADC_Input = PA1_DCtrl_1 ? driverinvsel_11_out : 1'bz;  // Driver driver_7
  assign driverinvsel_8_out = ~PA1_DCtrl_1 ? PA1_Output : 1'bz;  // DriverInvSel driverinvsel_8
  assign driverinvsel_8_out = PA1_DCtrl_1 ? PA1_A_Output : 1'bz;  // Driver driver_8
  assign PA3_Input = ~PA3_DCtrl_1 ? driverinvsel_12_out : 1'bz;  // DriverInvSel driverinvsel_9
  assign PA3_ADC_Input = PA3_DCtrl_1 ? driverinvsel_12_out : 1'bz;  // Driver driver_9
  assign driverinvsel_10_out = ~PA3_DCtrl_1 ? PA3_Output : 1'bz;  // DriverInvSel driverinvsel_10
  assign driverinvsel_10_out = PA3_DCtrl_1 ? PA3_A_Output : 1'bz;  // Driver driver_10
  assign driverinvsel_11_out = ~PA1_DCtrl_0 ? in_45 : 1'bz;  // DriverInvSel driverinvsel_11
  assign out_46 = PA1_DCtrl_0 ? driverinvsel_8_out : 1'bz;  // Driver driver_11
  assign driverinvsel_12_out = ~PA3_DCtrl_0 ? in_47 : 1'bz;  // DriverInvSel driverinvsel_12
  assign out_48 = PA3_DCtrl_0 ? driverinvsel_10_out : 1'bz;  // Driver driver_12

  // Notes on the sheet:
  //   clk: Hz: 10
  //   Output Data Register
  //   Alternate Output Register
  //   Input Data Register
  //   ADC Input Register
  //   Control Dir Register
  //   P0
  //   P2
  //   Cada par de bits del registro de control (comenzando de izquierda a derecha)
  //   indica el modo de operación del respectivo pin. 00:entrada, 01:salida
  //   10: entrada análoga, 11:salida alternativa.
  //   P1
  //   P3
endmodule
