// Digital circuit timer.dig as structural Verilog
module timer (
  input  CK_INT,
  input  Timer_enable,
  input  D7,
  input  set,
  input  clear,
  input  D6,
  input  D5,
  input  D4,
  input  D3,
  input  D2,
  input  D1,
  input  D0,
  input  set_2,
  input  set_3,
  input  clear_2,
  output Overflow,
  output out_15,
  output out_16,
  output out_17,
  output out_18,
  output out_19,
  output out_20,
  output out_21,
  output Interrupt,
  output out_25,
  output out_26,
  output out_27,
  output out_28,
  output out_29,
  output out_30,
  output out_31,
  output out_32
);

  wire and_1_out, and_3_out, and_4_out, and_5_out, and_6_out, and_7_out, and_8_out, and_9_out, and_10_out,
       and_12_out, and_13_out, and_14_out, and_15_out, and_16_out, and_17_out, and_18_out, d_ff_as_1_q,
       d_ff_as_2_q, d_ff_as_4_q, d_ff_as_6_q, d_ff_as_8_q, d_ff_as_9_q, d_ff_as_11_q, d_ff_as_13_q,
       d_ff_as_15_q, multiplexer_1_out, multiplexer_2_out, multiplexer_3_out, multiplexer_4_out,
       multiplexer_5_out, multiplexer_6_out, multiplexer_7_out, multiplexer_8_out, multiplexer_9_out,
       multiplexer_10_out, multiplexer_11_out, multiplexer_12_out, multiplexer_13_out, multiplexer_14_out,
       multiplexer_15_out, multiplexer_16_out, multiplexer_17_out, multiplexer_18_out, multiplexer_19_out,
       multiplexer_20_out, multiplexer_21_out, multiplexer_22_out, multiplexer_23_out, multiplexer_24_out,
       xnor_1_out, xnor_2_out, xnor_3_out, xnor_4_out, xnor_5_out, xnor_6_out, xnor_7_out, xnor_8_out,
       xor_1_out, xor_2_out, xor_3_out, xor_4_out, xor_5_out, xor_6_out, xor_7_out, xor_8_out, xor_9_out,
       xor_10_out, xor_11_out, xor_12_out, xor_13_out, xor_14_out, xor_15_out, xor_16_out;

  and and_1 (and_1_out, Timer_enable, CK_INT);
  and and_2 (Overflow, d_ff_as_1_q, and_3_out);
  xor xor_1 (xor_1_out, d_ff_as_1_q, and_3_out);
  Multiplexer multiplexer_1 (.sel(Timer_enable), .in_0(d_ff_as_1_q), .in_1(xor_1_out), .out(multiplexer_1_out));
  D_FF_AS d_ff_as_1 (.Set(set_2), .D(multiplexer_1_out), .C(and_1_out), .Clr(and_10_out), .Q(d_ff_as_1_q));  // open: nQ
  Multiplexer multiplexer_2 (.sel(Timer_enable), .in_0(d_ff_as_2_q), .in_1(D7), .out(multiplexer_2_out));
  and and_3 (and_3_out, out_15, and_4_out);
  D_FF_AS d_ff_as_2 (.Set(set), .D(multiplexer_2_out), .C(and_1_out), .Clr(clear), .Q(d_ff_as_2_q));  // open: nQ
  xor xor_2 (xor_2_out, out_15, and_4_out);
  Multiplexer multiplexer_3 (.sel(Timer_enable), .in_0(out_15), .in_1(xor_2_out), .out(multiplexer_3_out));
  D_FF_AS d_ff_as_3 (.Set(set_2), .D(multiplexer_3_out), .C(and_1_out), .Clr(and_10_out), .Q(out_15));  // open: nQ
  Multiplexer multiplexer_4 (.sel(Timer_enable), .in_0(d_ff_as_4_q), .in_1(D6), .out(multiplexer_4_out));
  D_FF_AS d_ff_as_4 (.Set(set), .D(multiplexer_4_out), .C(and_1_out), .Clr(clear), .Q(d_ff_as_4_q));  // open: nQ
  and and_4 (and_4_out, out_16, and_5_out);
  xor xor_3 (xor_3_out, out_16, and_5_out);
  Multiplexer multiplexer_5 (.sel(Timer_enable), .in_0(out_16), .in_1(xor_3_out), .out(multiplexer_5_out));
  D_FF_AS d_ff_as_5 (.Set(set_2), .D(multiplexer_5_out), .C(and_1_out), .Clr(and_10_out), .Q(out_16));  // open: nQ
  Multiplexer multiplexer_6 (.sel(Timer_enable), .in_0(d_ff_as_6_q), .in_1(D5), .out(multiplexer_6_out));
  D_FF_AS d_ff_as_6 (.Set(set), .D(multiplexer_6_out), .C(and_1_out), .Clr(clear), .Q(d_ff_as_6_q));  // open: nQ
  and and_5 (and_5_out, out_17, and_6_out);
  xor xor_4 (xor_4_out, out_17, and_6_out);
  Multiplexer multiplexer_7 (.sel(Timer_enable), .in_0(out_17), .in_1(xor_4_out), .out(multiplexer_7_out));
  Multiplexer multiplexer_8 (.sel(Timer_enable), .in_0(d_ff_as_8_q), .in_1(D4), .out(multiplexer_8_out));
  D_FF_AS d_ff_as_7 (.Set(set_2), .D(multiplexer_7_out), .C(and_1_out), .Clr(and_10_out), .Q(out_17));  // open: nQ
  D_FF_AS d_ff_as_8 (.Set(set), .D(multiplexer_8_out), .C(and_1_out), .Clr(clear), .Q(d_ff_as_8_q));  // open: nQ
  and and_6 (and_6_out, out_18, and_7_out);
  xor xor_5 (xor_5_out, out_18, and_7_out);
  Multiplexer multiplexer_9 (.sel(Timer_enable), .in_0(out_18), .in_1(xor_5_out), .out(multiplexer_9_out));
  Multiplexer multiplexer_10 (.sel(Timer_enable), .in_0(d_ff_as_9_q), .in_1(D3), .out(multiplexer_10_out));
  D_FF_AS d_ff_as_9 (.Set(set), .D(multiplexer_10_out), .C(and_1_out), .Clr(clear), .Q(d_ff_as_9_q));  // open: nQ
  D_FF_AS d_ff_as_10 (.Set(set_2), .D(multiplexer_9_out), .C(and_1_out), .Clr(and_10_out), .Q(out_18));  // open: nQ
  Multiplexer multiplexer_11 (.sel(Timer_enable), .in_0(d_ff_as_11_q), .in_1(D2), .out(multiplexer_11_out));
  and and_7 (and_7_out, out_19, and_8_out);
  xor xor_6 (xor_6_out, out_19, and_8_out);
  Multiplexer multiplexer_12 (.sel(Timer_enable), .in_0(out_19), .in_1(xor_6_out), .out(multiplexer_12_out));
  D_FF_AS d_ff_as_11 (.Set(set), .D(multiplexer_11_out), .C(and_1_out), .Clr(clear), .Q(d_ff_as_11_q));  // open: nQ
  D_FF_AS d_ff_as_12 (.Set(set_2), .D(multiplexer_12_out), .C(and_1_out), .Clr(and_10_out), .Q(out_19));  // open: nQ
  Multiplexer multiplexer_13 (.sel(Timer_enable), .in_0(d_ff_as_13_q), .in_1(D1), .out(multiplexer_13_out));
  D_FF_AS d_ff_as_13 (.Set(set), .D(multiplexer_13_out), .C(and_1_out), .Clr(clear), .Q(d_ff_as_13_q));  // open: nQ
  and and_8 (and_8_out, out_20, and_9_out);
  xor xor_7 (xor_7_out, out_20, and_9_out);
  Multiplexer multiplexer_14 (.sel(Timer_enable), .in_0(out_20), .in_1(xor_7_out), .out(multiplexer_14_out));
  D_FF_AS d_ff_as_14 (.Set(set_2), .D(multiplexer_14_out), .C(and_1_out), .Clr(and_10_out), .Q(out_20));  // open: nQ
  Multiplexer multiplexer_15 (.sel(Timer_enable), .in_0(d_ff_as_15_q), .in_1(D0), .out(multiplexer_15_out));
  D_FF_AS d_ff_as_15 (.Set(set), .D(multiplexer_15_out), .C(and_1_out), .Clr(clear), .Q(d_ff_as_15_q));  // open: nQ
  and and_9 (and_9_out, out_21, Timer_enable);
  xor xor_8 (xor_8_out, out_21, Timer_enable);
  Multiplexer multiplexer_16 (.sel(Timer_enable), .in_0(out_21), .in_1(xor_8_out), .out(multiplexer_16_out));
  D_FF_AS d_ff_as_16 (.Set(set_2), .D(multiplexer_16_out), .C(and_1_out), .Clr(and_10_out), .Q(out_21));  // open: nQ
  xnor xnor_1 (xnor_1_out, d_ff_as_2_q, d_ff_as_1_q);
  xnor xnor_2 (xnor_2_out, d_ff_as_4_q, out_15);
  xnor xnor_3 (xnor_3_out, d_ff_as_6_q, out_16);
  xnor xnor_4 (xnor_4_out, d_ff_as_8_q, out_17);
  xnor xnor_5 (xnor_5_out, d_ff_as_9_q, out_18);
  xnor xnor_6 (xnor_6_out, d_ff_as_11_q, out_19);
  xnor xnor_7 (xnor_7_out, d_ff_as_13_q, out_20);
  xnor xnor_8 (xnor_8_out, d_ff_as_15_q, out_21);
  and and_10 (and_10_out, Timer_enable, xnor_1_out, xnor_2_out, xnor_3_out, xnor_4_out, xnor_5_out, xnor_6_out, xnor_7_out, xnor_8_out);
  and and_11 (Interrupt, out_25, and_12_out);
  xor xor_9 (xor_9_out, out_25, and_12_out);
  Multiplexer multiplexer_17 (.sel(Timer_enable), .in_0(out_25), .in_1(xor_9_out), .out(multiplexer_17_out));
  D_FF_AS d_ff_as_17 (.Set(set_3), .D(multiplexer_17_out), .C(and_10_out), .Clr(clear_2), .Q(out_25));  // open: nQ
  and and_12 (and_12_out, out_26, and_13_out);
  xor xor_10 (xor_10_out, out_26, and_13_out);
  Multiplexer multiplexer_18 (.sel(Timer_enable), .in_0(out_26), .in_1(xor_10_out), .out(multiplexer_18_out));
  D_FF_AS d_ff_as_18 (.Set(set_3), .D(multiplexer_18_out), .C(and_10_out), .Clr(clear_2), .Q(out_26));  // open: nQ
  and and_13 (and_13_out, out_27, and_14_out);
  xor xor_11 (xor_11_out, out_27, and_14_out);
  Multiplexer multiplexer_19 (.sel(Timer_enable), .in_0(out_27), .in_1(xor_11_out), .out(multiplexer_19_out));
  D_FF_AS d_ff_as_19 (.Set(set_3), .D(multiplexer_19_out), .C(and_10_out), .Clr(clear_2), .Q(out_27));  // open: nQ
  and and_14 (and_14_out, out_28, and_15_out);
  xor xor_12 (xor_12_out, out_28, and_15_out);
  Multiplexer multiplexer_20 (.sel(Timer_enable), .in_0(out_28), .in_1(xor_12_out), .out(multiplexer_20_out));
  D_FF_AS d_ff_as_20 (.Set(set_3), .D(multiplexer_20_out), .C(and_10_out), .Clr(clear_2), .Q(out_28));  // open: nQ
  and and_15 (and_15_out, out_29, and_16_out);
  xor xor_13 (xor_13_out, out_29, and_16_out);
  Multiplexer multiplexer_21 (.sel(Timer_enable), .in_0(out_29), .in_1(xor_13_out), .out(multiplexer_21_out));
  D_FF_AS d_ff_as_21 (.Set(set_3), .D(multiplexer_21_out), .C(and_10_out), .Clr(clear_2), .Q(out_29));  // open: nQ
  and and_16 (and_16_out, out_30, and_17_out);
  xor xor_14 (xor_14_out, out_30, and_17_out);
  Multiplexer multiplexer_22 (.sel(Timer_enable), .in_0(out_30), .in_1(xor_14_out), .out(multiplexer_22_out));
  D_FF_AS d_ff_as_22 (.Set(set_3), .D(multiplexer_22_out), .C(and_10_out), .Clr(clear_2), .Q(out_30));  // open: nQ
  and and_17 (and_17_out, out_31, and_18_out);
  xor xor_15 (xor_15_out, out_31, and_18_out);
  Multiplexer multiplexer_23 (.sel(Timer_enable), .in_0(out_31), .in_1(xor_15_out), .out(multiplexer_23_out));
  D_FF_AS d_ff_as_23 (.Set(set_3), .D(multiplexer_23_out), .C(and_10_out), .Clr(clear_2), .Q(out_31));  // open: nQ
  and and_18 (and_18_out, out_32, Timer_enable);
  xor xor_16 (xor_16_out, out_32, Timer_enable);
  Multiplexer multiplexer_24 (.sel(Timer_enable), .in_0(out_32), .in_1(xor_16_out), .out(multiplexer_24_out));
  D_FF_AS d_ff_as_24 (.Set(set_3), .D(multiplexer_24_out), .C(and_10_out), .Clr(clear_2), .Q(out_32));  // open: nQ

  // Notes on the sheet:
  //   Las señales que ingresan al timer son la señal de activación (EN) y la señal
  //   de reloj, lo anterior, junto a la información que hay en el data register, es todo
  //   lo que necesita el timer para funcionar. Note que la activar el timer activamos
  //   tambien el DATA REGISTER y los contadores. Note también que la señal de 
  //   reloj de los registros y los contadores solo se activa si la entrada del
  //   timer enable está en alto.
  //   CONTADOR1
  //   DATA REGISTER (8bits)
  //   El registro contador 1, al activarse el timer enable, comienza a contar 
  //   incrementandose en 1 por cada señal de reloj. Al ser de 8bits cuenta 
  //   hasta 255.
  //   En el DATA REGISTER se guarda el valor del prescaler, al ser de 8bits
  //   se puede ingresar un valor X (entero) entre 255 y 1, lo que se busca es
  //    que la frencuencia de la señal de salida de la comparación entre el
  //    CONTADOR1 y el data register tenga un periodo X veces mayor que la
  //   de la señal de reloj, o lo que es lo mismo una frencuencia x veces más
  //   baja.
  //   El COMPARDOR es un conjunto de compuertas NXOR las cuales 
  //   son 1 si y solo si ambas entradas estan en 1. Estas 8 compuertas
  //   NXOR se conectan a una compuerta AND la cual tiene 9 entradas.
  //   La razon de esta novena entrada es debido a que si solo tiene 8
  //   al iniciar el programa  y activar la señal de reloj el comparador
  //    lanzaría un 1 inmediatamente, pues se tiene 0 en el CONTADOR1  
  //   y en el DATA REGISTER, por lo que el CONTADOR2 se 
  //   incrementaría, lo cual no debe pasar. Otra factor importante que se
  //   tuvo en cuenta es el reinicio del CONTADOR1, el cual se debe 
  //   reiniciar cada vez que el prescaler manda una señal, es decir
  //   cuando la salida del comaparador es 1, por lo cual la salida
  //   de la compuerta AND es conectador al clear del CONTADOR1.
  //   COMPARADOR
  //   CONTADOR2
  //   El registro CONTADOR2, es el encargado de generar la señal de interrupción cuando se deborde, este se 
  //   incrementa cada vez que a la salida del comparador se tiene un 1, como se observa para llevar a cabo se
  //   conecta la señal salida del comparador a la señal de reloj del CONTADOR2
endmodule
